# Fritzing sketch xbee_display (saved by Fritzing 0.6.2b)

parts:
  Componente1 = XBee Explorer Regulated
  U1 = mystery part, 3 pins [chip_label="7 segment display (serial)" spacing=300mil]
  VCC1 = obsolete Battery
  U2 = XBee  # not connected

nets:
  N1: Componente1.DOUT, U1.pin1
  N2: Componente1.5V, U1.pin2, VCC1.+
  N3: Componente1.GND, U1.pin3, VCC1.-
